# Fritzing sketch base_station (saved by Fritzing 0.8.3b)

parts:
  RaspberryPi1 = Raspberry Pi Model B
  U1 = V_REG_LD1117VXX [package=78xxl]
  JACK1 = 2.1mm DC Barrel Jack
  C1 = Electrolytic Capacitor [capacitance=47µF package="200 mil [THT, electrolytic]"]
  C2 = Electrolytic Capacitor [capacitance=47µF package="200 mil [THT, electrolytic]"]
  KEYPAD1 = Membrane Matrix Keypad
  U2 = LCD-16X2 [package=lcd-16x2_noholes]

nets:
  3V3: RaspberryPi1.3V3, U2.VDD
  N1: RaspberryPi1.SDA, U2.A
  N2: RaspberryPi1.SCL, U2.DB7
  GND: RaspberryPi1.GND, U2.VSS, U2.R_W, U2.K
  N3: RaspberryPi1.#4, U2.DB6
  N4: RaspberryPi1.TXD, KEYPAD1.1
  N5: RaspberryPi1.RXD, KEYPAD1.2
  N6: RaspberryPi1.#17, U2.DB5
  N7: RaspberryPi1.#18, KEYPAD1.3
  N8: RaspberryPi1.#21, U2.DB4
  N9: RaspberryPi1.#22, U2.E
  N10: RaspberryPi1.#23, KEYPAD1.4
  N11: RaspberryPi1.#24, KEYPAD1.5
  N12: RaspberryPi1.MOSI, U2.RS
  N13: RaspberryPi1.#25, KEYPAD1.6
  N14: RaspberryPi1.CS0, KEYPAD1.7
  N15: U1.OUT, C2.+
  GND_2: U1.GND, JACK1.sleeve, C1.-, C2.-
  N16: U1.IN, JACK1.center

custom parts:
  Raspberry Pi Model B: Raspberry Pi (Model B)
  2.1mm DC Barrel Jack: 2.1mm DC Barrel Jack with Thru-Hole Connectors (breadboardable)
  Membrane Matrix Keypad: Membrane Matrix 3x4 Keypad
