# Fritzing sketch camera_module (saved by Fritzing 0.8.3b)
breadboards: 1

parts:
  U1 = atmega328 [package=dip]
  R1 = Resistor [tolerance=±5% resistance=10k package=THT]
  C7 = Capacitor [part_number="22 pF" package=cap-pth-5mm]
  XTAL2 = Crystal [frequency="16 Mhz" package=SMD]
  C8 = Capacitor [part_number="22 pF" package=cap-pth-5mm]
  CAMERA1 = TTL Serial JPEG Camera
  microSD1 = MicroSD Breakout
  R2 = Resistor [tolerance=±5% resistance=10k package=THT]
  R3 = Resistor [tolerance=±5% resistance=10k package=THT]
  U2 = V_REG_LD1117VXX [package=78xxl]
  JACK2 = 2.1mm DC Barrel Jack
  C9 = Electrolytic Capacitor [capacitance=47µF package="200 mil [THT, electrolytic]"]
  C10 = Electrolytic Capacitor [capacitance=47µF package="200 mil [THT, electrolytic]"]

nets:
  N1: U1.RESET, R1.Pin_1
  N2: U1.D0_(RX), R2.Pin_0
  N3: U1.D1_(TX), CAMERA1.TX
  5V: U1.VCC, U1.AVCC, U1.AREF, R1.Pin_0, CAMERA1.5V, microSD1.5V, U2.OUT, C9.+
  GND: U1.GND, C7.2, C8.2, CAMERA1.GND, microSD1.GND, R3.Pin_0, U2.GND, JACK2.sleeve, C9.-, C10.-
  N4: U1.XLAT1, C7.1, XTAL2.pin_1
  N5: U1.XLAT2, XTAL2.pin_0, C8.1
  N6: U1.D10_(PWM), microSD1.CS
  N7: U1.D11_(PWM), microSD1.DI
  N8: U1.D12, microSD1.DO
  N9: U1.D13, microSD1.CLK
  N10: CAMERA1.RX, R2.Pin_1, R3.Pin_1
  N11: U2.IN, JACK2.center, C10.+

custom parts:
  TTL Serial JPEG Camera: TTL Serial JPEG Camera with NTSC Out
  MicroSD Breakout: 5V-ready microSD Breakout with Level Shifter
  2.1mm DC Barrel Jack: 2.1mm DC Barrel Jack with Thru-Hole Connectors (breadboardable)
