# Fritzing sketch contact_sensor (saved by Fritzing 0.8.3b)
breadboards: 1

parts:
  U1 = atmega328 [package=dip]
  R1 = Resistor [tolerance=±5% resistance=10k package=THT]
  Battery = Battery
  C4 = Electrolytic Capacitor [capacitance=10µF package="200 mil [THT, electrolytic]"]
  C7 = Capacitor [part_number="22 pF" package=cap-pth-5mm]
  XTAL2 = Crystal [frequency="16 Mhz" package=SMD]
  C8 = Capacitor [part_number="22 pF" package=cap-pth-5mm]
  S1 = Pushbutton [package=THT]
  R2 = Resistor [tolerance=±5% resistance=10k package=THT]

nets:
  N1: U1.RESET, R1.Pin_1
  N2: U1.VCC, U1.AVCC, U1.AREF, R1.Pin_0, Battery.+, C4.+, S1.leg0
  GND: U1.GND, Battery.-, C4.-, C7.2, C8.2, R2.Pin_1
  N3: U1.XLAT1, C7.1, XTAL2.pin_1
  N4: U1.XLAT2, XTAL2.pin_0, C8.1
  N5: U1.D7, S1.leg1, R2.Pin_0
