# Fritzing sketch motion_sensor (saved by Fritzing 0.8.2b)
breadboards: 1

parts:
  U1 = atmega328 [package=dip]
  R1 = Resistor [tolerance=±5% resistance=10k package=THT]
  Battery = Battery
  C4 = Electrolytic Capacitor [capacitance=10µF package="200 mil [THT, electrolytic]"]
  PIR1 = PIR sensor
  C7 = Capacitor [part_number="22 pF" package=cap-pth-5mm]
  C8 = Capacitor [part_number="22 pF" package=cap-pth-5mm]
  XTAL2 = Crystal [frequency="16 Mhz" package=SMD]

nets:
  N1: U1.RESET, R1.Pin_1
  VCC: U1.VCC, U1.AVCC, U1.AREF, R1.Pin_0, Battery.+, C4.+, PIR1.VDD
  GND: U1.GND, Battery.-, C4.-, PIR1.GND, C7.1, C8.2
  N2: U1.XLAT1, C7.2, XTAL2.pin_1
  N3: U1.XLAT2, C8.1, XTAL2.pin_0
  N4: U1.D7, PIR1.SIG
