# Fritzing sketch relay_control (saved by Fritzing 0.8.3b)
breadboards: 1

parts:
  U1 = atmega328 [package=dip]
  R1 = Resistor [tolerance=±5% resistance=10k package=THT]
  C7 = Capacitor [part_number="22 pF" package=cap-pth-5mm]
  C8 = Capacitor [part_number="22 pF" package=cap-pth-5mm]
  XTAL2 = Crystal [frequency="16 Mhz" package=SMD]
  U2 = RELAY [package=relay-jzc]
  U3 = Voltage Regulator - 5V [package="DPak [SMD]"]
  C9 = Electrolytic Capacitor [capacitance=10µF package="200 mil [THT, electrolytic]"]
  C10 = Electrolytic Capacitor [capacitance=10µF package="200 mil [THT, electrolytic]"]
  U4 = Transformer [package=transformer]
  D1 = Rectifier Diode [part_number=1N4001 package="300 mil [THT]"]
  D2 = Rectifier Diode [part_number=1N4001 package="300 mil [THT]"]
  D3 = Rectifier Diode [part_number=1N4001 package="300 mil [THT]"]
  D4 = Rectifier Diode [part_number=1N4001 package="300 mil [THT]"]
  JP1 = Header 3 [package=screwterminal-3.5mm-3_lock.007s]
  JP2 = Header 3 [package=screwterminal-3.5mm-3_lock.007s]

nets:
  N1: U1.RESET, R1.Pin_1
  N2: U1.VCC, U1.AVCC, U1.AREF, R1.Pin_0, U3.output_voltage, C9.+
  GND: U1.GND, C7.1, C8.2, U2.COIL2, U3.GND, C9.-, C10.-, D1.anode, D3.anode
  N3: U1.XLAT1, C7.2, XTAL2.pin_1
  N4: U1.XLAT2, C8.1, XTAL2.pin_0
  N5: U1.D7, U2.COIL1
  N6: U2.NO, JP2.3
  N7: U2.MAIN, U4.1, JP1.3
  N8: U3.input_voltage, C10.+, D2.cathode, D4.cathode
  N9: U4.2, JP1.1, JP2.1
  N10: U4.3, D3.cathode, D4.anode
  N11: U4.4, D1.cathode, D2.anode
