# Fritzing sketch temperature_sensor_digital (saved by Fritzing 0.8.3b)
breadboards: 1

parts:
  U1 = atmega328 [package=dip]
  R1 = Resistor [tolerance=±5% resistance=10k package=THT]
  C4 = Electrolytic Capacitor [capacitance=10µF package="200 mil [THT, electrolytic]"]
  DHT1 = DHT11 Humitidy and Temperature Sensor
  R2 = Resistor [tolerance=±5% resistance=10k package=THT]
  C7 = Capacitor [part_number="22 pF" package=cap-pth-5mm]
  XTAL2 = Crystal [frequency="16 Mhz" package=SMD]
  C8 = Capacitor [part_number="22 pF" package=cap-pth-5mm]
  Battery = Battery

nets:
  N1: U1.RESET, R1.Pin_1
  VCC: U1.VCC, U1.AVCC, U1.AREF, R1.Pin_0, C4.+, DHT1.VDD, R2.Pin_0, Battery.+
  GND: U1.GND, C4.-, DHT1.GND, C7.2, C8.2, Battery.-
  N2: U1.XLAT1, C7.1, XTAL2.pin_1
  N3: U1.XLAT2, XTAL2.pin_0, C8.1
  N4: U1.D7, DHT1.DATA, R2.Pin_1

custom parts:
  DHT11 Humitidy and Temperature Sensor: DHT11 Humidity and Temperature Sensor
